// Logisim project ALU.circ as structural Verilog: 2 circuits, main circuit main
module main (
  input  [15:0] in_1,
  input  [15:0] in_2
);

  ALU alu_1 ();  // open: in_1, in_2, Op_Selector, in_3
endmodule

module ALU (
  input  [15:0] in_1,
  input  [15:0] in_2,
  input  [15:0] in_3,
  input  [2:0] Op_Selector
);

  wire button_1_out;
  wire [15:0] adder_1_out, and_1_out, divider_1_out, or_1_out, shifter_1_out, shifter_2_out, subtractor_1_out;

  Adder #(.width(16)) adder_1 (.a(in_1), .b(in_2), .out(adder_1_out));  // open: cin, cout
  Subtractor #(.width(16)) subtractor_1 (.a(in_1), .b(in_2), .out(subtractor_1_out));  // open: bin, bout
  Multiplier #(.width(16)) multiplier_1 (.a(in_1), .b(in_2), .out(subtractor_1_out));  // open: cin, cout
  Divider #(.width(16)) divider_1 (.a(in_1), .b(in_2), .out(divider_1_out));  // open: upper, rem
  assign and_1_out = in_1 & in_2;  // AND_Gate and_1, 16 bits wide
  assign or_1_out = in_1 | in_2;  // OR_Gate or_1, 16 bits wide
  Shifter #(.width(16), .shift("lr")) shifter_1 (.in(in_1), .\dist (in_2[3:0]), .out(shifter_1_out));
  Shifter #(.width(16)) shifter_2 (.in(in_1), .\dist (in_2[3:0]), .out(shifter_2_out));
  Multiplexer #(.select(3), .width(16)) multiplexer_1 (
    .in0(adder_1_out), .in1(subtractor_1_out), .in2(subtractor_1_out), .in3(divider_1_out),
    .in4(shifter_1_out), .in5(shifter_2_out), .in6(and_1_out), .in7(or_1_out), .out(in_3), .sel(Op_Selector),
    .en(button_1_out));
  Button button_1 (.out(button_1_out));

  // Notes on the sheet:
  //   Op1
  //   Op2
  //   Enable
  //   ALU Output
endmodule
