// Logisim project ALU.circ as structural Verilog: 2 circuits, main circuit main
module main (
  input  [15:0] in_1,
  input  [15:0] in_2,
  input  [3:0] in_3
);

  wire [15:0] undriven;

  ALU alu_1 (.Op1(in_1), .Op2(in_2), .Op_Selector(in_3), .ALU_Output(undriven));
endmodule

module ALU (
  input  [15:0] Op1,
  input  [15:0] Op2,
  input  [15:0] ALU_Output,
  input  [3:0] Op_Selector
);

  wire comparator_1_eq, comparator_1_gt, comparator_1_lt, Enable_out;
  wire [15:0] adder_1_out, and_1_out, bit_extender_1_out, bit_extender_2_out, bit_extender_3_out,
       divider_1_out, or_1_out, shifter_1_out, shifter_2_out, subtractor_1_out;

  Adder #(.width(16)) adder_1 (.a(Op1), .b(Op2), .out(adder_1_out));  // open: cin, cout
  Subtractor #(.width(16)) subtractor_1 (.a(Op1), .b(Op2), .out(subtractor_1_out));  // open: bin, bout
  Multiplier #(.width(16)) multiplier_1 (.a(Op1), .b(Op2), .out(subtractor_1_out));  // open: cin, cout
  Divider #(.width(16)) divider_1 (.a(Op1), .b(Op2), .out(divider_1_out));  // open: upper, rem
  assign and_1_out = Op1 & Op2;  // AND_Gate and_1, 16 bits wide
  assign or_1_out = Op1 | Op2;  // OR_Gate or_1, 16 bits wide
  Comparator #(.width(16), .mode("unsigned")) comparator_1 (
    .a(Op1), .b(Op2), .gt(comparator_1_gt), .eq(comparator_1_eq), .lt(comparator_1_lt));
  Shifter #(.width(16), .shift("lr")) shifter_1 (.in(Op1), .\dist (Op2[3:0]), .out(shifter_1_out));
  Shifter #(.width(16)) shifter_2 (.in(Op1), .\dist (Op2[3:0]), .out(shifter_2_out));
  assign bit_extender_1_out = {{15{1'b0}}, comparator_1_gt};  // Bit_Extender bit_extender_1
  assign bit_extender_2_out = {{15{1'b0}}, comparator_1_eq};  // Bit_Extender bit_extender_2
  assign bit_extender_3_out = {{15{1'b0}}, comparator_1_lt};  // Bit_Extender bit_extender_3
  Multiplexer #(.select(4), .width(16)) multiplexer_1 (
    .in0(adder_1_out), .in1(subtractor_1_out), .in2(subtractor_1_out), .in3(divider_1_out),
    .in4(shifter_2_out), .in5(shifter_1_out), .in6(and_1_out), .in7(or_1_out), .in8(bit_extender_1_out),
    .in9(bit_extender_2_out), .in10(bit_extender_3_out), .in11({16{1'b0}}), .in12({16{1'b0}}),
    .in13({16{1'b0}}), .in14({16{1'b0}}), .in15({16{1'b0}}), .out(ALU_Output), .sel(Op_Selector),
    .en(Enable_out));
  Button Enable (.out(Enable_out));
endmodule
