// Logisim project controller.circ as structural Verilog: 1 circuit, main circuit main
module main (
  input  [3:0] in_1,
  output bra,
  output branch,
  output regWrite,
  output regDst,
  output AluSrc,
  output MemR,
  output MenW
);

  wire add_out, and_out, boz_out, comp_out, div_out, ls_out, multiply_out, or_out, rs_out, stri_out,
       subtract_out;

  and load (MemR, ~in_1[3], ~in_1[2], ~in_1[1], ~in_1[0]);  // AND_Gate
  and add (add_out, ~in_1[3], ~in_1[2], ~in_1[1], in_1[0]);  // AND_Gate
  and store (MenW, ~in_1[3], ~in_1[2], in_1[1], ~in_1[0]);  // AND_Gate
  and subtract (subtract_out, ~in_1[3], ~in_1[2], in_1[1], in_1[0]);  // AND_Gate
  and stri (stri_out, ~in_1[3], in_1[2], ~in_1[1], ~in_1[0]);  // AND_Gate
  and multiply (multiply_out, ~in_1[3], in_1[2], ~in_1[1], in_1[0]);  // AND_Gate
  and boz (boz_out, ~in_1[3], in_1[2], in_1[1], ~in_1[0]);  // AND_Gate
  and div (div_out, ~in_1[3], in_1[2], in_1[1], in_1[0]);  // AND_Gate
  and u_bra (bra, in_1[3], ~in_1[2], ~in_1[1], ~in_1[0]);  // AND_Gate
  and \and  (and_out, in_1[3], ~in_1[2], ~in_1[1], in_1[0]);  // AND_Gate
  and ls (ls_out, in_1[3], in_1[2], ~in_1[2], in_1[0]);  // AND_Gate
  and \or  (or_out, in_1[3], ~in_1[2], in_1[1], in_1[0]);  // AND_Gate
  and rs (rs_out, in_1[3], in_1[2], in_1[1], in_1[0]);
  and comp (comp_out, in_1[3], ~in_1[2], in_1[1], ~in_1[0]);  // AND_Gate
  or or_2 (branch, boz_out, bra);
  or or_3 (regWrite, in_1[0], comp_out, MemR, stri_out);
  or or_4 (regDst, comp_out, MemR, add_out, subtract_out, multiply_out, div_out, and_out, or_out, ls_out, rs_out);
  or or_5 (AluSrc, MemR, MenW, stri_out);
endmodule
