// Logisim project ALU.circ as structural Verilog: 1 circuit, main circuit main
module main (
  input  [15:0] In1,
  input  [15:0] In2,
  input  [3:0] OpCode,
  output [15:0] ALU_out
);

  wire comparator_1_gt;
  wire [15:0] adder_1_out, and_1_out, bit_extender_1_out, divider_1_out, multiplier_1_out, or_1_out,
       shifter_1_out, shifter_2_out, subtractor_1_out;

  Adder #(.width(16)) adder_1 (.a(In1), .b(In2), .out(adder_1_out));  // open: cin, cout
  Subtractor #(.width(16)) subtractor_1 (.a(In1), .b(In2), .out(subtractor_1_out));  // open: bin, bout
  Multiplier #(.width(16)) multiplier_1 (.a(In1), .b(In2), .out(multiplier_1_out));  // open: cin, cout
  Divider #(.width(16)) divider_1 (.a(In1), .b(In2), .out(divider_1_out));  // open: upper, rem
  assign and_1_out = In1 & In2;  // AND_Gate and_1, 16 bits wide
  Comparator #(.width(16)) comparator_1 (.a(In1), .b(In2), .gt(comparator_1_gt));  // open: eq, lt
  assign or_1_out = In1 | In2;  // OR_Gate or_1, 16 bits wide
  Shifter #(.width(16)) shifter_1 (.in(In1), .\dist (In2[3:0]), .out(shifter_1_out));
  Shifter #(.width(16), .shift("lr")) shifter_2 (.in(In1), .\dist (In2[3:0]), .out(shifter_2_out));
  assign bit_extender_1_out = {{15{1'b0}}, comparator_1_gt};  // Bit_Extender bit_extender_1
  Multiplexer #(.select(4), .width(16), .disabled(0), .enable("false")) multiplexer_1 (
    .in0({16{1'b0}}), .in1(adder_1_out), .in2({16{1'b0}}), .in3(subtractor_1_out), .in4({16{1'b0}}),
    .in5(multiplier_1_out), .in6({16{1'b0}}), .in7(divider_1_out), .in8({16{1'b0}}), .in9(and_1_out),
    .in10(bit_extender_1_out), .in11(or_1_out), .in12({16{1'b0}}), .in13(shifter_1_out), .in14({16{1'b0}}),
    .in15(shifter_2_out), .out(ALU_out), .sel(OpCode));
endmodule
