// Logisim project CtrlUnit.circ as structural Verilog: 1 circuit, main circuit main
module main (
  input  [3:0] OpCode,
  output boz,
  output MemToReg,
  output branch,
  output regWrite,
  output RegDes,
  output AluSrc,
  output MemR,
  output MemW,
  output notStri
);

  wire bra_out, comp_out, stri_out;

  and load (MemR, ~OpCode[3], ~OpCode[2], ~OpCode[1], ~OpCode[0]);  // AND_Gate
  and store (MemW, ~OpCode[3], ~OpCode[2], OpCode[1], ~OpCode[0]);  // AND_Gate
  and stri (stri_out, ~OpCode[3], OpCode[2], ~OpCode[1], ~OpCode[0]);  // AND_Gate
  and u_boz (boz, ~OpCode[3], OpCode[2], OpCode[1], ~OpCode[0]);  // AND_Gate
  and bra (bra_out, OpCode[3], ~OpCode[2], ~OpCode[1], ~OpCode[0]);  // AND_Gate
  and comp (comp_out, OpCode[3], ~OpCode[2], OpCode[1], ~OpCode[0]);  // AND_Gate
  not not_1 (notStri, stri_out);
  or or_1 (branch, boz, bra_out);
  or or_2 (regWrite, OpCode[0], comp_out, stri_out, MemR);
  and and_1 (RegDes, ~stri_out, ~MemW, ~MemR);  // AND_Gate
  or or_3 (AluSrc, stri_out, MemW, MemR);

  assign MemToReg = MemR;
endmodule
