// Logisim project Register File 2.0.circ as structural Verilog: 1 circuit, main circuit main
module main (
  input  RegWrite,
  input  [3:0] Rd,
  input  [15:0] WriteData,
  input  [3:0] Rs,
  input  [3:0] Rt,
  input  Clock,
  output [15:0] Rs_Data,
  output [15:0] Rt_Data
);

  wire demultiplexer_1_out0, demultiplexer_1_out1, demultiplexer_1_out2, demultiplexer_1_out3,
       demultiplexer_1_out4, demultiplexer_1_out5, demultiplexer_1_out6, demultiplexer_1_out7,
       demultiplexer_1_out8, demultiplexer_1_out9, demultiplexer_1_out10, demultiplexer_1_out11,
       demultiplexer_1_out12, demultiplexer_1_out13, demultiplexer_1_out14, demultiplexer_1_out15;
  wire [15:0] register_1_q, register_2_q, register_3_q, register_4_q, register_5_q, register_6_q,
       register_7_q, register_8_q, register_9_q, register_10_q, register_11_q, register_12_q, register_13_q,
       register_14_q, register_15_q, register_16_q;

  Demultiplexer #(.select(4), .enable("false")) demultiplexer_1 (
    .out0(demultiplexer_1_out0), .out1(demultiplexer_1_out1), .out2(demultiplexer_1_out2),
    .out3(demultiplexer_1_out3), .out4(demultiplexer_1_out4), .out5(demultiplexer_1_out5),
    .out6(demultiplexer_1_out6), .out7(demultiplexer_1_out7), .out8(demultiplexer_1_out8),
    .out9(demultiplexer_1_out9), .out10(demultiplexer_1_out10), .out11(demultiplexer_1_out11),
    .out12(demultiplexer_1_out12), .out13(demultiplexer_1_out13), .out14(demultiplexer_1_out14),
    .out15(demultiplexer_1_out15), .in(RegWrite), .sel(Rd));
  Register #(.width(16)) register_1 (
    .D(WriteData), .en(demultiplexer_1_out0), .Q(register_1_q), .clk(Clock));  // open: clr
  Register #(.width(16)) register_2 (
    .D(WriteData), .en(demultiplexer_1_out1), .Q(register_2_q), .clk(Clock));  // open: clr
  Register #(.width(16)) register_3 (
    .D(WriteData), .en(demultiplexer_1_out2), .Q(register_3_q), .clk(Clock));  // open: clr
  Register #(.width(16)) register_4 (
    .D(WriteData), .en(demultiplexer_1_out3), .Q(register_4_q), .clk(Clock));  // open: clr
  Register #(.width(16)) register_5 (
    .D(WriteData), .en(demultiplexer_1_out4), .Q(register_5_q), .clk(Clock));  // open: clr
  Register #(.width(16)) register_6 (
    .D(WriteData), .en(demultiplexer_1_out5), .Q(register_6_q), .clk(Clock));  // open: clr
  Register #(.width(16)) register_7 (
    .D(WriteData), .en(demultiplexer_1_out6), .Q(register_7_q), .clk(Clock));  // open: clr
  Register #(.width(16)) register_8 (
    .D(WriteData), .en(demultiplexer_1_out7), .Q(register_8_q), .clk(Clock));  // open: clr
  Register #(.width(16)) register_9 (
    .D(WriteData), .en(demultiplexer_1_out8), .Q(register_9_q), .clk(Clock));  // open: clr
  Register #(.width(16)) register_10 (
    .D(WriteData), .en(demultiplexer_1_out9), .Q(register_10_q), .clk(Clock));  // open: clr
  Register #(.width(16)) register_11 (
    .D(WriteData), .en(demultiplexer_1_out10), .Q(register_11_q), .clk(Clock));  // open: clr
  Register #(.width(16)) register_12 (
    .D(WriteData), .en(demultiplexer_1_out11), .Q(register_12_q), .clk(Clock));  // open: clr
  Register #(.width(16)) register_13 (
    .D(WriteData), .en(demultiplexer_1_out12), .Q(register_13_q), .clk(Clock));  // open: clr
  Register #(.width(16)) register_14 (
    .D(WriteData), .en(demultiplexer_1_out13), .Q(register_14_q), .clk(Clock));  // open: clr
  Register #(.width(16)) register_15 (
    .D(WriteData), .en(demultiplexer_1_out14), .Q(register_15_q), .clk(Clock));  // open: clr
  Register #(.width(16)) register_16 (
    .D(WriteData), .en(demultiplexer_1_out15), .Q(register_16_q), .clk(Clock));  // open: clr
  Multiplexer #(.select(4), .width(16), .enable("false")) multiplexer_1 (
    .in0(register_1_q), .in1(register_2_q), .in2(register_3_q), .in3(register_4_q), .in4(register_5_q),
    .in5(register_6_q), .in6(register_7_q), .in7(register_8_q), .in8(register_9_q), .in9(register_10_q),
    .in10(register_11_q), .in11(register_12_q), .in12(register_13_q), .in13(register_14_q),
    .in14(register_15_q), .in15(register_16_q), .out(Rs_Data), .sel(Rs));
  Multiplexer #(.select(4), .width(16), .enable("false")) multiplexer_2 (
    .in0(register_1_q), .in1(register_2_q), .in2(register_3_q), .in3(register_4_q), .in4(register_5_q),
    .in5(register_6_q), .in6(register_7_q), .in7(register_8_q), .in8(register_9_q), .in9(register_10_q),
    .in10(register_11_q), .in11(register_12_q), .in12(register_13_q), .in13(register_14_q),
    .in14(register_15_q), .in15(register_16_q), .out(Rt_Data), .sel(Rt));
endmodule
